# Fritzing sketch Power Measurement Schematic (saved by Fritzing 0.9.3b)
breadboards: 1

parts:
  A1 = 1x18650 battery shield [package=THT]
  U1 = LuaNode32 / ESP32 [part_number=ESP32S-PIN30]
  Part1 = Adafruit INA219 [part_number="Adafruit #904"]
  U2 = ESP8266 NodeMCU LoLin module
  A2 = 1x18650 battery shield [package=THT]
  U3 = LuaNode32 / ESP32 [part_number=ESP32S-PIN30]
  Part2 = Adafruit INA219 [part_number="Adafruit #904"]

nets:
  N1: A1.pin_9, A1.pin_11, Part1.VIN+
  GND: A1.pin_10, A1.pin_12, U1.GND, Part1.GND, U2.GND
  3V3: U1.3V3, Part1.VCC
  N2: U1.D21, Part1.SDA
  N3: U1.D22, Part1.SCL
  N4: Part1.VIN-, U2.Vin
  N5: A2.pin_9, A2.pin_11, Part2.VIN+
  GND_2: A2.pin_10, A2.pin_12, U3.GND, Part2.GND
  3V3_2: U3.3V3, Part2.VCC
  N6: U3.D21, Part2.SDA
  N7: U3.D22, Part2.SCL

custom parts:
  1x18650 battery shield: 1x18650 Lithium Battery Shield V3 CC CV Type-C Micro USB Mobile Power Bank DIY Module 5V 3A 3V 1A for iPhone Samsung Xiaomi.
  LuaNode32 / ESP32: New Image for LuaNode32 DOIT ESP32 DEVKIT V1. Base parts from LuaNode32 / ESP32 ESP32 based LuaNode32 by G.Noorlander DOIT Esp32 DevKit v1 (30 pins long, 11 pins width) by Werner Rothschopf (modified by vanepp Dec 2018)
  Adafruit INA219: This breakout board will solve all your power-monitoring problems. Instead of struggling with two multimeters, you can just use the handy INA219B chip on this breakout to both measure both the high side voltage and DC current draw over I2C with 1% precision. Most current-measuring devices such as our current panel meter are only good for low side measuring. That means that unless you want to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
  ESP8266 NodeMCU LoLin module: ESP8266 based NodeMCU
