# Fritzing sketch System Schematic (saved by Fritzing 0.9.3b)
breadboards: 1

parts:
  U1 = ESP8266 NodeMCU LoLin module
  DHT1 = DHT22 Humidity and Temperature Sensor
  U2 = ESP8266 NodeMCU LoLin module
  Part1 = MicroSD Card Module

nets:
  N1: U1.D4, DHT1.DATA
  3V3: U1.3V3, DHT1.VDD
  GND: U1.GND, DHT1.GND
  3V3_2: U2.3V3, Part1.VCC
  N2: U2.D5, Part1.SCK
  N3: U2.D6, Part1.MISO
  N4: U2.D7, Part1.MOSI
  N5: U2.D8, Part1.CS
  GND_2: U2.GND, Part1.GND

custom parts:
  ESP8266 NodeMCU LoLin module: ESP8266 based NodeMCU
